# Fritzing sketch Untitled Sketch (saved by Fritzing 0.9.3b)
circuit board: 6cm x 6cm
breadboards: 2

parts:
  TB6612 = Motor Driver 1A Dual TB6612FNG [part_number=ROB_09457]
  NRF24L01+ = NRF24L01+ Breakout Board
  J2 = male pin header, 3 pins [form="♂ (male)"]  # not connected
  J3 = male pin header, 5 pins [form="♂ (male)"]
  VinA = Screw terminal - 2 pins [package=THT]
  VinM = Screw terminal - 2 pins [package=THT]
  Motor = screw terminal, 4 pins
  J1 = male pin header, 3 pins [form="♂ (male)"]  # not connected
  Arduino_Nano_V3_0 = Arduino Nano (Rev3.0)

nets:
  N1: TB6612.PWMA, Arduino_Nano_V3_0.D3
  N2: TB6612.AIN2, Arduino_Nano_V3_0.D2
  N3: TB6612.AIN1, Arduino_Nano_V3_0.D4
  N4: TB6612.STBY, Arduino_Nano_V3_0.A7
  N5: TB6612.BIN1, Arduino_Nano_V3_0.D7
  N6: TB6612.BIN2, Arduino_Nano_V3_0.D8
  N7: TB6612.PWMB, Arduino_Nano_V3_0.D9
  N8: TB6612.VM, VinM.pin2
  VCC: TB6612.VCC, Arduino_Nano_V3_0.5V
  N9: TB6612.A01, Motor.pin4
  N10: TB6612.A02, Motor.pin3
  N11: TB6612.B02, Motor.pin2
  N12: TB6612.B01, Motor.pin1
  GND: TB6612.GND#15, NRF24L01+.GND, J3.pin1, J3.pin5, VinA.pin2, VinM.pin1, Arduino_Nano_V3_0.GND
  VCC_2: NRF24L01+.VCC, Arduino_Nano_V3_0.3V3
  N13: NRF24L01+.CE, Arduino_Nano_V3_0.A0
  N14: NRF24L01+.CS, Arduino_Nano_V3_0.A1
  N15: NRF24L01+.MOSI, Arduino_Nano_V3_0.D11/MOSI
  N16: J3.pin2, Arduino_Nano_V3_0.D5
  N17: J3.pin3, Arduino_Nano_V3_0.D6
  N18: J3.pin4, Arduino_Nano_V3_0.D10
  N19: VinA.pin1, Arduino_Nano_V3_0.VIN

notes:
  + -

custom parts:
  Motor Driver 1A Dual TB6612FNG: The TB6612FNG motor driver can control up to two DC motors at a constant current of 1.2A (3.2A peak). Two input signals (IN1 and IN2) can be used to control the motor in one of four function modes - CW, CCW, short-brake, and stop. The two motor outputs (A and B) can be separately controlled, the speed of each motor is controlled via a PWM input signal with a frequency up to 100kHz. The STBY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
