# Fritzing sketch V1.0 (saved by Fritzing 0.9.3b)
circuit board: 6cm x 6cm
breadboards: 2

parts:
  TB6612 = Motor Driver 1A Dual TB6612FNG [part_number=ROB_09457]
  NRF24L01+ = NRF24L01+ Breakout Board
  VinA = Screw terminal - 2 pins [package=THT]
  VinM = Screw terminal - 2 pins [package=THT]
  Motor = screw terminal, 4 pins
  Arduino_Nano_V3_0 = Arduino Nano (Rev3.0)
  J3 = female pin header, 5 pins [form="♀ (female)"]
  J1 = female pin header, 5 pins [form="♀ (female)"]

nets:
  N1: TB6612.PWMA, Arduino_Nano_V3_0.D3
  N2: TB6612.AIN2, Arduino_Nano_V3_0.D2
  N3: TB6612.AIN1, Arduino_Nano_V3_0.D4
  N4: TB6612.STBY, Arduino_Nano_V3_0.A2
  N5: TB6612.BIN1, Arduino_Nano_V3_0.D7
  N6: TB6612.BIN2, Arduino_Nano_V3_0.D8
  N7: TB6612.PWMB, Arduino_Nano_V3_0.D9
  N8: TB6612.VM, VinM.pin2
  VCC: TB6612.VCC, Arduino_Nano_V3_0.5V
  GND: TB6612.GND#10, NRF24L01+.GND, VinA.pin2, Arduino_Nano_V3_0.GND, J3.pin1, J3.pin5
  N9: TB6612.A01, Motor.pin4
  N10: TB6612.A02, Motor.pin3
  N11: TB6612.B02, Motor.pin2
  N12: TB6612.B01, Motor.pin1
  N13: TB6612.GND#15, VinM.pin1
  VCC_2: NRF24L01+.VCC, Arduino_Nano_V3_0.3V3
  N14: NRF24L01+.CE, Arduino_Nano_V3_0.A0
  N15: NRF24L01+.CS, Arduino_Nano_V3_0.A1
  N16: NRF24L01+.SCK, Arduino_Nano_V3_0.D13/SCK
  N17: NRF24L01+.MOSI, Arduino_Nano_V3_0.D11/MOSI
  N18: NRF24L01+.MISO, Arduino_Nano_V3_0.D12/MISO
  N19: VinA.pin1, Arduino_Nano_V3_0.VIN
  N20: Arduino_Nano_V3_0.D5, J3.pin2
  N21: Arduino_Nano_V3_0.D6, J3.pin3
  N22: Arduino_Nano_V3_0.D10, J3.pin4
  N23: Arduino_Nano_V3_0.A7, J1.pin1
  N24: Arduino_Nano_V3_0.A6, J1.pin2
  N25: Arduino_Nano_V3_0.A5, J1.pin3
  N26: Arduino_Nano_V3_0.A4, J1.pin4
  N27: Arduino_Nano_V3_0.A3, J1.pin5

notes:
  + -

custom parts:
  Motor Driver 1A Dual TB6612FNG: The TB6612FNG motor driver can control up to two DC motors at a constant current of 1.2A (3.2A peak). Two input signals (IN1 and IN2) can be used to control the motor in one of four function modes - CW, CCW, short-brake, and stop. The two motor outputs (A and B) can be separately controlled, the speed of each motor is controlled via a PWM input signal with a frequency up to 100kHz. The STBY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
